// Logisim project rcd.circ as structural Verilog: 1 circuit, main circuit main
module main (
);

  wire clock_1_out;
  wire [7:0] counter_1_q;

  Clock clock_1 (.out(clock_1_out));
  Counter counter_1 (.Q(counter_1_q), .clk(clock_1_out));  // open: load, D, count, carry, clr
  ROM rom_1 (.addr(counter_1_q));  // open: data, sel
  RAM ram_1 (.clk(clock_1_out));  // open: addr, data, sel, ld, clr
endmodule
